# Fritzing sketch breadboard (saved by Fritzing 0.9.3b)
breadboards: 6

parts:
  MCU = IC, DIP package, 40 pins [chip_label="Atmega 162"]
  RESET = Pushbutton [package="[SMD]"]
  LED = LED - 3mm [color="Red (633nm)" package="3 mm [THT]"]
  C2 = Capacitor [package=cap-pth-large]
  VCC1 = Battery block 9V
  C3 = Capacitor [package=cap-pth-small]
  U1 = Voltage Regulator - 5V [package="TO220 [THT]"]

nets:
  N1: MCU.pin1, LED.anode
  N2: MCU.pin9, RESET.Pin_1, RESET.Pin_2
  5V: MCU.pin39, C2.1, U1.output_voltage
  GND: MCU.pin40, RESET.Pin_3, RESET.Pin_4, LED.cathode, C2.2, VCC1.-, C3.2, U1.GND
  N3: VCC1.+, C3.1, U1.input_voltage
